# Fritzing sketch ButtonRead (saved by Fritzing 0.9.3b)
breadboards: 1

parts:
  Part3 = Arduino Uno (Rev3)
  S1 = Pushbutton [package="[SMD]"]
  J3 = Basic Servo
  J4 = female pin header, 3 pins [form="♀ (female)"]

nets:
  N1: Part3.A0, S1.Pin_1, S1.Pin_2
  N2: Part3.D10_PWM/SS, J3.pulse, J4.pin1
  5V: Part3.5V, J3.vcc, J4.pin2
  GND: Part3.GND, S1.Pin_3, S1.Pin_4, J3.gnd, J4.pin3
