# Fritzing sketch LDR_LED (saved by Fritzing 0.9.3b)
breadboards: 1

parts:
  Part4 = Arduino Uno (Rev3)
  R1 = Resistor [tolerance=±5% resistance=220 package=THT]
  R2 = Photocell (LDR) [package=THT]
  LED1 = LED - 5mm [color="Red (633nm)" package="5 mm [THT]"]

nets:
  N1: Part4.A0, R1.Pin_0, R2.pin_1
  N2: Part4.D3_PWM, LED1.anode
  N3: Part4.5V, R2.pin_0
  N4: Part4.GND, R1.Pin_1, LED1.cathode
