# Fritzing sketch MicroServo (saved by Fritzing 0.9.3b)
breadboards: 1

parts:
  Part2 = Arduino Uno (Rev3)
  J1 = Basic Servo
  J2 = female pin header, 3 pins [form="♀ (female)"]

nets:
  N1: Part2.D10_PWM/SS, J1.pulse, J2.pin1
  5V: Part2.5V, J1.vcc, J2.pin2
  GND: Part2.GND, J1.gnd, J2.pin3
