# Fritzing sketch PotServo (saved by Fritzing 0.9.3b)
breadboards: 1

parts:
  Part4 = Arduino Uno (Rev3)
  J5 = Basic Servo
  J6 = female pin header, 3 pins [form="♀ (female)"]
  R1 = Rotary Potentiometer (Small) [maximum_resistance=100kΩ package=THT]

nets:
  N1: Part4.A0, R1.wiper
  N2: Part4.D10_PWM/SS, J5.pulse, J6.pin1
  5V: Part4.5V, J5.vcc, J6.pin2, R1.leg2
  GND: Part4.GND, J5.gnd, J6.pin3, R1.leg1
