# Fritzing sketch ServoWithIRComms (saved by Fritzing 0.9.3b)
breadboards: 1

parts:
  Part3 = Arduino Uno (Rev3)
  J3 = Basic Servo
  J4 = female pin header, 3 pins [form="♀ (female)"]
  IR2 = TSOP312.., 314.. [package=THT]

nets:
  N1: Part3.D10_PWM/SS, J3.pulse, J4.pin1
  N2: Part3.D3_PWM, IR2.GND
  5V: Part3.5V, J3.vcc, J4.pin2, IR2.Data
  GND: Part3.GND, J3.gnd, J4.pin3, IR2.Vs
