# Fritzing sketch ServoWithPot (saved by Fritzing 0.9.3b)
breadboards: 1

parts:
  Part3 = Arduino Uno (Rev3)
  J3 = Basic Servo
  J4 = female pin header, 3 pins [form="♀ (female)"]
  R1 = Rotary Potentiometer (Small) [maximum_resistance=100kΩ package=THT]
  R2 = Resistor [tolerance=±5% resistance=220 package=THT]
  R3 = Resistor [tolerance=±5% resistance=220 package=THT]

nets:
  N1: Part3.A0, R3.Pin_1
  N2: Part3.D10_PWM/SS, J3.pulse, J4.pin1
  5V: Part3.5V, J3.vcc, J4.pin2, R1.leg2
  VIN: Part3.VIN, J3.gnd, J4.pin3, R2.Pin_1
  N3: R1.leg1, R2.Pin_0
  N4: R1.wiper, R3.Pin_0
