# Fritzing sketch TempSensor (saved by Fritzing 0.9.3b)
breadboards: 1

parts:
  Part5 = Arduino Uno (Rev3)
  T1 = LM35 Temperature Sensor [package="TO92 [THT]"]

nets:
  N1: Part5.A0, T1.Vout
  N2: Part5.5V, T1.+Vs
  GND: Part5.GND, T1.GND
