# Fritzing sketch TwoButtonController (saved by Fritzing 0.9.3b)
breadboards: 1

parts:
  Part4 = Arduino Uno (Rev3)
  S2 = Pushbutton [package="[SMD]"]
  S3 = Pushbutton [package="[SMD]"]

nets:
  N1: Part4.A0, S2.Pin_1, S2.Pin_2
  N2: Part4.A1, S3.Pin_1, S3.Pin_2
  N3: Part4.GND, S2.Pin_3, S2.Pin_4, S3.Pin_3, S3.Pin_4
