# Fritzing sketch TwoButtonControllerWithLED (saved by Fritzing 0.9.3b)
breadboards: 1

parts:
  Part5 = Arduino Uno (Rev3)
  S4 = Pushbutton [package="[SMD]"]
  S5 = Pushbutton [package="[SMD]"]
  LED1 = LED - 5mm [color="Red (633nm)" package="5 mm [THT]"]
  R1 = Resistor [tolerance=±5% resistance=220 package=THT]

nets:
  N1: Part5.A0, S5.Pin_1, S5.Pin_2
  N2: Part5.A1, S4.Pin_1, S4.Pin_2
  N3: Part5.D3_PWM, LED1.anode
  N4: Part5.GND, S4.Pin_3, S4.Pin_4, S5.Pin_3, S5.Pin_4, R1.Pin_1
  N5: LED1.cathode, R1.Pin_0
